# Fritzing sketch breadboard (saved by Fritzing 0.9.3b)
breadboards: 1
stripboards: 12

parts:
  U2 = ESP8266 WiFi Module [part_number=ESP8266]
  LED1 = smd LED [color="Red (660nm)" package="0805 [SMD]"]
  R1 = Resistor [tolerance=±5% resistance=1k package="2512 [SMD]"]
  LED2 = smd LED [color="Green (570nm)" package="0805 [SMD]"]
  R2 = Resistor [tolerance=±5% resistance=1k package="2512 [SMD]"]
  R3 = Resistor [tolerance=±5% resistance=6.8k package="2512 [SMD]"]
  R4 = Resistor [tolerance=±5% resistance=6.8k package="2512 [SMD]"]
  J1 = female pin header, 4 pins [form="♀ (female)"]
  J2 = female pin header, 4 pins [form="♀ (female)"]
  J5 = Generic female header - 4 pins [form="♀ (female)" package=THT]  # not connected
  J6 = Generic female header - 3 pins [form="♀ (female)" package=THT]  # not connected
  J7 = Camdenboss CTB0158-2 [part_number=CTB0158-2 package=THT]  # not connected
  J8 = Camdenboss CTB0158-2 [part_number=CTB0158-2 package=THT]  # not connected
  J9 = female pin header, 2 pins [form="♀ (female)"]  # not connected
  J10 = female pin header, 2 pins [form="♀ (female)"]  # not connected
  J11 = female pin header, 2 pins [form="♀ (female)"]
  J12 = female pin header, 2 pins [form="♀ (female)"]
  J13 = Camdenboss CTB0158-2 [part_number=CTB0158-2 package=THT]
  J14 = female pin header, 2 pins [form="♀ (female)"]
  J15 = female pin header, 2 pins [form="♀ (female)"]
  J16 = female pin header, 2 pins [form="♀ (female)"]
  J17 = female pin header, 2 pins [form="♀ (female)"]
  U4 = ESP8266 WiFi Module [part_number=ESP8266]
  D1 = Rectifier Diode [part_number=1N4001 package="300 mil [THT]"]
  R7 = Vertical Resistor [tolerance=±5% resistance=10k package=THT]
  R8 = Vertical Resistor [tolerance=±5% resistance=10k package=THT]
  S5 = Pushbutton [package="[THT]"]
  J18 = Camdenboss CTB0158-2 [part_number=CTB0158-2 package=THT]  # not connected
  R9 = Vertical Resistor [tolerance=±5% resistance=1k package=THT]
  LED3 = smd LED [color="Red (660nm)" package="0805 [SMD]"]
  LED4 = smd LED [color="Green (570nm)" package="0805 [SMD]"]
  R10 = Vertical Resistor [tolerance=±5% resistance=1k package=THT]
  J19 = female pin header, 4 pins [form="♀ (female)"]
  J20 = female pin header, 4 pins [form="♀ (female)"]
  J21 = Camdenboss CTB0158-2 [part_number=CTB0158-2 package=THT]
  J22 = Camdenboss CTB0158-2 [part_number=CTB0158-2 package=THT]
  J26 = female pin header, 2 pins [form="♀ (female)"]
  U5 = ESP8266 WiFi Module [part_number=ESP8266]
  D2 = Rectifier Diode [part_number=1N4001 package="300 mil [THT]"]
  R11 = Vertical Resistor [tolerance=±5% resistance=1k package=THT]
  R12 = Vertical Resistor [tolerance=±5% resistance=1k package=THT]
  LED5 = smd LED [color="Red (660nm)" package="0805 [SMD]"]
  LED6 = smd LED [color="Green (570nm)" package="0805 [SMD]"]
  J27 = female pin header, 4 pins [form="♀ (female)"]
  J28 = female pin header, 4 pins [form="♀ (female)"]
  J24 = female pin header, 1 pin [form="♀ (female)"]
  J25 = female pin header, 2 pins [form="♀ (female)"]
  J23 = female pin header, 1 pin [form="♀ (female)"]
  J29 = female pin header, 3 pins [form="♀ (female)"]  # not connected
  J30 = female pin header, 4 pins [form="♀ (female)"]
  R17 = Resistor Mini [tolerance=±5% resistance=10k package=THT]
  J31 = female pin header, 1 pin [form="♀ (female)"]  # not connected
  J32 = female pin header, 1 pin [form="♀ (female)"]  # not connected
  R18 = Resistor Mini [tolerance=±5% resistance=10k package=THT]
  R19 = Vertical Resistor [tolerance=±5% resistance=1M package=THT]
  J33 = Camdenboss CTB0158-2 [part_number=CTB0158-2 package=THT]
  J34 = Camdenboss CTB0158-2 [part_number=CTB0158-2 package=THT]  # not connected
  J35 = Camdenboss CTB0158-2 [part_number=CTB0158-2 package=THT]
  J36 = female pin header, 2 pins [form="♀ (female)"]
  U6 = ESP8266 WiFi Module [part_number=ESP8266]  # not connected
  R20 = Vertical Resistor [tolerance=±5% resistance=1k package=THT]
  R21 = Vertical Resistor [tolerance=±5% resistance=1k package=THT]
  J37 = female pin header, 4 pins [form="♀ (female)"]
  J38 = female pin header, 4 pins [form="♀ (female)"]
  J39 = female pin header, 2 pins [form="♀ (female)"]
  J40 = female pin header, 4 pins [form="♀ (female)"]  # not connected
  J41 = female pin header, 1 pin [form="♀ (female)"]
  J42 = female pin header, 3 pins [form="♀ (female)"]  # not connected
  J43 = female pin header, 1 pin [form="♀ (female)"]  # not connected
  J44 = female pin header, 1 pin [form="♀ (female)"]
  J45 = female pin header, 1 pin [form="♀ (female)"]  # not connected
  R22 = Resistor Mini [tolerance=±5% resistance=1k package=THT]
  R23 = Resistor Mini [tolerance=±5% resistance=1k package=THT]
  LED7 = smd LED [color="Green (570nm)" package="0805 [SMD]"]
  J46 = Camdenboss CTB0158-2 [part_number=CTB0158-2 package=THT]
  D12 = Small signal Diode flat 300mil [part_number=1N4148 package="300 mil [THT]"]
  R25 = Resistor Mini [tolerance=±5% resistance=10k package=THT]
  C1 = Electrolytic Capacitor [capacitance=220µF package="100 mil [THT, electrolytic]"]
  C2 = Ceramic Capacitor [capacitance=100nF package="100 mil [THT, multilayer]"]
  LED9 = LED Red 5mm - Top View [package="5 mm [THT] Top View"]
  R26 = Resistor Mini [tolerance=±5% resistance=1k package=THT]

nets:
  N1: U2.RXD, U2.VCC, J1.pin1, J2.pin1
  N2: U2.GPIO_0, U2.RST, J1.pin2, J2.pin2
  N3: U2.GPIO_2, U2.CH_PD, J1.pin3, J2.pin3
  N4: U2.GND, U2.TXD, J1.pin4, J2.pin4
  N5: LED1.anode, R1.Pin_1
  N6: R1.Pin_0, R2.Pin_0
  N7: LED2.anode, R2.Pin_1
  N8: R3.Pin_0, R4.Pin_0
  N9: J11.pin1, J11.pin2, J12.pin1, J12.pin2
  N10: J13.pin1, J16.pin1, J16.pin2, J17.pin1, J17.pin2
  N11: J13.pin2, D1.cathode
  N12: J14.pin1, J14.pin2
  N13: J15.pin1, J15.pin2
  N14: U4.RXD, J19.pin1
  N15: U4.VCC, R7.Pin_1, R8.Pin_1, J20.pin1
  N16: U4.GPIO_0, R9.Pin_1, J19.pin2
  N17: U4.RST, S5.Pin_3, S5.Pin_4, J20.pin2
  N18: U4.GPIO_2, R10.Pin_1, J19.pin3
  N19: U4.CH_PD, R7.Pin_0, J20.pin3
  N20: U4.GND, LED3.anode, LED4.anode, J19.pin4
  N21: U4.TXD, R8.Pin_0, J20.pin4
  N22: S5.Pin_1, S5.Pin_2
  N23: R9.Pin_0, LED3.cathode
  N24: LED4.cathode, R10.Pin_0
  N25: J21.pin1, J21.pin2
  N26: J22.pin1, U5.GND, R11.Pin_1, R12.Pin_1, J27.pin1, J33.pin2
  N27: J22.pin2, D2.anode
  N28: J26.pin1, J26.pin2
  N29: U5.RXD, J27.pin4, J30.pin2
  N30: U5.VCC, J28.pin4, R17.Pin_1, R18.Pin_1, R19.Pin_1
  N31: U5.GPIO_0, LED5.anode, J27.pin3
  N32: U5.RST, J28.pin3, R18.Pin_0
  N33: U5.GPIO_2, LED6.anode, J27.pin2, R19.Pin_0
  N34: U5.CH_PD, J28.pin2, R17.Pin_0
  N35: U5.TXD, J28.pin1, J33.pin1
  N36: R11.Pin_0, LED5.cathode
  N37: R12.Pin_0, LED6.cathode
  N38: J24.pin1, J23.pin1
  N39: J25.pin1, J25.pin2
  N40: J35.pin1, R26.Pin_0
  N41: J35.pin2, R20.Pin_1, J38.pin1, J46.pin1, C1.-, C2.0
  N42: J36.pin1, J36.pin2
  N43: R20.Pin_0, LED7.cathode
  N44: R21.Pin_0, LED9.cathode
  N45: J37.pin1, R26.Pin_1
  N46: J37.pin2, R23.Pin_0
  N47: J37.pin3, R22.Pin_0
  N48: J37.pin4, R22.Pin_1, R23.Pin_1, R25.Pin_0, C1.+, C2.1
  N49: J38.pin2, LED7.anode
  N50: J38.pin3, R25.Pin_1, LED9.anode
  N51: J39.pin1, J39.pin2
  N52: J41.pin1, J44.pin1
  N53: J46.pin2, D12.anode

notes:
  Reset
  Data in, 38400 baud
  Bottom two 1-pin headers are actually mounting posts.
  Lower right breadboard is a proxy for the 3.3V RS485 converter board. Upper right mini breadboard is a proxy for the 3.3V power supply.
  Because both of these will be raised up by headers, (as is the ESP01) wires can run underneath.
  At the top are a pair of screw terminals for +12V and Gnd. At the bottom on the right are the A and B terminals for the RS485 signal from the radio.
  The "reset" button on the upper left is probably not necessary (esp because the ESP-01 can be removed for reprogramming)
  Vcc Tx Rx GND
  A B GND
  OUT+          +IN
  Reset Button
  External Reset
  Top two 1-pin headers are actually mounting posts.
  Upper breadboard is a proxy for the 3.3V RS485 converter board. lower left mini breadboard is a proxy for the 3.3V power supply.
  Because both of these will be raised up by headers, (as is the ESP01) wires can run underneath.
  At the top left are the A and B terminals for the RS485 signal from the radio. The "A" terminal should connect to the brown GX220 wire; the "B" should connect to the grey one.
  At the bottom left are a pair of screw terminals for +12V and Gnd. At bottom center are a pair of terminal for a "reset" button (see doc'n). These pins also provide debugging output at 38400 baud during normal operation.

custom parts:
  ESP8266 WiFi Module: Generic WiFi Module based on the ESP8266 with onboard PCB antenna and UART communications
  Generic female header - 4 pins: Generic female header
  Generic female header - 3 pins: Generic female header
  Vertical Resistor: A generic resistor (0.25W)
  Resistor Mini: A generic resistor (0.25W)
  Small signal Diode flat 300mil: Small signal diode such as the 1n4148 Footprint: mounted flat on 300mil centers.
  LED Red 5mm - Top View: A generic red LED (~1.8V)

// code stored in the sketch: Untitled2.ino

